# Fritzing sketch eightbutton (saved by Fritzing 0.9.3b)
breadboards: 1

parts:
  Part1 = Arduino Uno (Rev3)
  R1 = Resistor [tolerance=±5% resistance=10k package=THT]
  < = Pushbutton [package="[THT]"]
  R2 = Resistor [tolerance=±5% resistance=10k package=THT]
  v = Pushbutton [package="[THT]"]
  ^ = Pushbutton [package="[THT]"]
  > = Pushbutton [package="[THT]"]
  SRT = Pushbutton [package="[THT]"]
  R3 = Resistor [tolerance=±5% resistance=10k package=THT]
  R4 = Resistor [tolerance=±5% resistance=10k package=THT]
  R5 = Resistor [tolerance=±5% resistance=10k package=THT]
  A = Pushbutton [package="[THT]"]
  SEL = Pushbutton [package="[THT]"]
  B = Pushbutton [package="[THT]"]
  R6 = Resistor [tolerance=±5% resistance=10k package=THT]
  R7 = Resistor [tolerance=±5% resistance=10k package=THT]
  R8 = Resistor [tolerance=±5% resistance=10k package=THT]

nets:
  N1: Part1.D10_PWM/SS, >.Pin_1, >.Pin_2, R4.Pin_0
  N2: Part1.D11_PWM/MOSI, v.Pin_1, v.Pin_2, R3.Pin_0
  N3: Part1.D12/MISO, R2.Pin_0, ^.Pin_1, ^.Pin_2
  N4: Part1.D13/SCK, R1.Pin_0, <.Pin_1, <.Pin_2
  N5: Part1.D4, B.Pin_1, B.Pin_2, R8.Pin_0
  N6: Part1.D5_PWM, A.Pin_1, A.Pin_2, R6.Pin_0
  N7: Part1.D6_PWM, SRT.Pin_1, SRT.Pin_2, R5.Pin_0
  N8: Part1.D7, SEL.Pin_1, SEL.Pin_2, R7.Pin_0
  N9: Part1.5V, <.Pin_3, <.Pin_4, v.Pin_3, v.Pin_4, ^.Pin_3, ^.Pin_4, >.Pin_3, >.Pin_4, SRT.Pin_3, SRT.Pin_4, SEL.Pin_3, SEL.Pin_4
  N10: Part1.GND, R1.Pin_1, R2.Pin_1, R3.Pin_1, R4.Pin_1, R5.Pin_1, R7.Pin_1
  N11: A.Pin_3, A.Pin_4, B.Pin_3, B.Pin_4
  N12: R6.Pin_1, R8.Pin_1
