# Fritzing sketch onebutton (saved by Fritzing 0.9.3b)
breadboards: 1

parts:
  Part1 = Arduino Uno (Rev3)
  R1 = Resistor [tolerance=±5% resistance=10k package=THT]
  S1 = Pushbutton [package="[THT]"]  # not connected

nets:
  N1: Part1.D2, R1.Pin_1
